// Logisim project MIPS CPU V2.circ as structural Verilog
module main (
  input  [31:0] in_1,
  input  [23:0] in_2
);

  wire and_1_out, button_1_out, clock_1_out, cpu_1_write, not_1_out, or_1_out, or_2_out;
  wire [1:0] cpu_1_data_size;
  wire [2:0] pull_resistor_1_node;
  wire [7:0] controlled_buffer_1_out, controlled_buffer_2_out, controlled_buffer_3_out, pull_resistor_2_node;
  wire [23:0] shifter_1_out;
  wire [31:0] cpu_1_data_out, multiplier_1_cout, multiplier_1_out, ram_1_data, shifter_2_out;

  Button button_1 (.out(button_1_out));
  Clock clock_1 (.out(clock_1_out));
  // Probe on in_2
  CPU cpu_1 (
    .reset(button_1_out), .Data_in(ram_1_data), .\wait (or_1_out), .Data_out(cpu_1_data_out),
    .clock(clock_1_out), .write(cpu_1_write), .Data_Size(cpu_1_data_size));  // open: trap, address, read
  or or_1 (or_1_out, in_2[0], in_2[1]);
  Shifter #(.width(24), .shift("lr")) shifter_1 (.in(in_2), .\dist (5'b00010), .out(shifter_1_out));
  not not_1 (not_1_out, or_1_out);
  RAM #(.addrWidth(24), .dataWidth(32), .bus("separate")) ram_1 (
    .addr(shifter_1_out), .din(in_1), .data(ram_1_data), .str(cpu_1_write), .sel(1'b1), .clk(clock_1_out),
    .ld(1'b1));  // open: clr
  Shifter #(.width(32)) shifter_2 (.in(32'h1), .\dist ({in_2[1:0], pull_resistor_1_node}), .out(shifter_2_out));
  Pull_Resistor pull_resistor_1 (.node({in_2[1:0], pull_resistor_1_node}));
  Multiplier #(.width(32)) multiplier_1 (
    .a(in_1), .b(shifter_2_out), .out(multiplier_1_out), .cout(multiplier_1_cout));  // open: cin
  // Probe on multiplier_1_out
  or or_2 (or_2_out, in_2[0], in_2[1]);
  assign controlled_buffer_1_out = or_2_out ? multiplier_1_cout[7:0] : 8'bz;  // Controlled_Buffer controlled_buffer_1
  assign controlled_buffer_2_out = in_2[1] ? multiplier_1_cout[15:8] : 8'bz;  // Controlled_Buffer controlled_buffer_2
  assign controlled_buffer_3_out = and_1_out ? multiplier_1_cout[23:16] : 8'bz;  // Controlled_Buffer controlled_buffer_3
  and and_1 (and_1_out, in_2[0], in_2[1]);
  // Probe on {pull_resistor_2_node, controlled_buffer_3_out, controlled_buffer_2_out, controlled_buffer_1_out}
  Pull_Resistor pull_resistor_2 (.node({pull_resistor_2_node, controlled_buffer_3_out, controlled_buffer_2_out, controlled_buffer_1_out}));
endmodule

module Registers (
  input  Clock,
  input  [31:0] d_Register_Input,
  input  Clear,
  input  write_register_d,
  input  write_register_t,
  input  write_register_s,
  input  [4:0] d_register_select,
  input  read_t_register,
  input  [4:0] t_Register_Select,
  input  [4:0] s_Register_Select,
  input  read_s_register,
  output [31:0] t_register_Ouput,
  output [31:0] s_register_Ouput
);

  wire demultiplexer_1_out0, demultiplexer_1_out1, demultiplexer_1_out2, demultiplexer_1_out3,
       demultiplexer_1_out4, demultiplexer_1_out5, demultiplexer_1_out6, demultiplexer_1_out7,
       demultiplexer_1_out8, demultiplexer_1_out9, demultiplexer_1_out10, demultiplexer_1_out11,
       demultiplexer_1_out12, demultiplexer_1_out13, demultiplexer_1_out14, demultiplexer_1_out15,
       demultiplexer_1_out16, demultiplexer_1_out17, demultiplexer_1_out18, demultiplexer_1_out19,
       demultiplexer_1_out20, demultiplexer_1_out21, demultiplexer_1_out22, demultiplexer_1_out23,
       demultiplexer_1_out24, demultiplexer_1_out25, demultiplexer_1_out26, demultiplexer_1_out27,
       demultiplexer_1_out28, demultiplexer_1_out29, demultiplexer_1_out30, demultiplexer_1_out31, or_1_out,
       register_output_select_1_out_3, register_output_select_1_out_4, register_output_select_1_out_5,
       register_output_select_1_out_6, register_output_select_1_out_7, register_output_select_1_out_8,
       register_output_select_1_out_9, register_output_select_1_out_10, register_output_select_2_out_3,
       register_output_select_2_out_4, register_output_select_2_out_5, register_output_select_2_out_6,
       register_output_select_2_out_7, register_output_select_2_out_8, register_output_select_2_out_9,
       register_output_select_2_out_10, register_output_select_3_out_3, register_output_select_3_out_4,
       register_output_select_3_out_5, register_output_select_3_out_6, register_output_select_3_out_7,
       register_output_select_3_out_8, register_output_select_3_out_9, register_output_select_3_out_10,
       register_output_select_4_out_3, register_output_select_4_out_4, register_output_select_4_out_5,
       register_output_select_4_out_6, register_output_select_4_out_7, register_output_select_4_out_8,
       register_output_select_4_out_9, register_output_select_4_out_10, register_output_select_5_out_3,
       register_output_select_5_out_4, register_output_select_5_out_5, register_output_select_5_out_6,
       register_output_select_5_out_7, register_output_select_5_out_8, register_output_select_5_out_9,
       register_output_select_5_out_10, register_output_select_6_out_3, register_output_select_6_out_4,
       register_output_select_6_out_5, register_output_select_6_out_6, register_output_select_6_out_7,
       register_output_select_6_out_8, register_output_select_6_out_9, register_output_select_6_out_10,
       register_output_select_7_out_3, register_output_select_7_out_4, register_output_select_7_out_5,
       register_output_select_7_out_6, register_output_select_7_out_7, register_output_select_7_out_8,
       register_output_select_7_out_9, register_output_select_7_out_10, register_output_select_8_out_3,
       register_output_select_8_out_4, register_output_select_8_out_5, register_output_select_8_out_6,
       register_output_select_8_out_7, register_output_select_8_out_8, register_output_select_8_out_9,
       register_output_select_8_out_10;
  wire [3:0] demultiplexer_2_out0, demultiplexer_2_out4, demultiplexer_2_out8, demultiplexer_2_out12,
       demultiplexer_2_out16, demultiplexer_2_out20, demultiplexer_2_out24, demultiplexer_2_out28,
       demultiplexer_3_out0, demultiplexer_3_out4, demultiplexer_3_out8, demultiplexer_3_out12,
       demultiplexer_3_out16, demultiplexer_3_out20, demultiplexer_3_out24, demultiplexer_3_out28;
  wire [4:0] controlled_buffer_1_out;

  or or_1 (or_1_out, write_register_d, write_register_t, write_register_s);
  Demultiplexer #(.select(5), .enable("false")) demultiplexer_1 (
    .out0(demultiplexer_1_out0), .out1(demultiplexer_1_out1), .out2(demultiplexer_1_out2),
    .out3(demultiplexer_1_out3), .out4(demultiplexer_1_out4), .out5(demultiplexer_1_out5),
    .out6(demultiplexer_1_out6), .out7(demultiplexer_1_out7), .out8(demultiplexer_1_out8),
    .out9(demultiplexer_1_out9), .out10(demultiplexer_1_out10), .out11(demultiplexer_1_out11),
    .out12(demultiplexer_1_out12), .out13(demultiplexer_1_out13), .out14(demultiplexer_1_out14),
    .out15(demultiplexer_1_out15), .out16(demultiplexer_1_out16), .out17(demultiplexer_1_out17),
    .out18(demultiplexer_1_out18), .out19(demultiplexer_1_out19), .out20(demultiplexer_1_out20),
    .out21(demultiplexer_1_out21), .out22(demultiplexer_1_out22), .out23(demultiplexer_1_out23),
    .out24(demultiplexer_1_out24), .out25(demultiplexer_1_out25), .out26(demultiplexer_1_out26),
    .out27(demultiplexer_1_out27), .out28(demultiplexer_1_out28), .out29(demultiplexer_1_out29),
    .out30(demultiplexer_1_out30), .out31(demultiplexer_1_out31), .in(or_1_out), .sel(controlled_buffer_1_out));
  assign controlled_buffer_1_out = write_register_d ? d_register_select : 5'bz;  // Controlled_Buffer controlled_buffer_1
  assign controlled_buffer_1_out = write_register_t ? t_Register_Select : 5'bz;  // Controlled_Buffer controlled_buffer_2
  assign controlled_buffer_1_out = write_register_s ? s_Register_Select : 5'bz;  // Controlled_Buffer controlled_buffer_3
  Pull_Resistor pull_resistor_1 (.node(controlled_buffer_1_out));
  register register_1 (
    .\input (d_Register_Input), .output_enable_1(register_output_select_1_out_6),
    .write(demultiplexer_1_out3), .clock(Clock), .clear(Clear), .out_2(s_register_Ouput),
    .out_1(t_register_Ouput), .output_enable_2(register_output_select_1_out_10));
  register register_2 (
    .\input (d_Register_Input), .output_enable_1(register_output_select_2_out_6),
    .write(demultiplexer_1_out7), .clock(Clock), .clear(Clear), .out_2(s_register_Ouput),
    .out_1(t_register_Ouput), .output_enable_2(register_output_select_2_out_10));
  register register_3 (
    .\input (d_Register_Input), .output_enable_1(register_output_select_3_out_6),
    .write(demultiplexer_1_out11), .clock(Clock), .clear(Clear), .out_2(s_register_Ouput),
    .out_1(t_register_Ouput), .output_enable_2(register_output_select_3_out_10));
  register register_4 (
    .\input (d_Register_Input), .output_enable_1(register_output_select_4_out_6),
    .write(demultiplexer_1_out15), .clock(Clock), .clear(Clear), .out_2(s_register_Ouput),
    .out_1(t_register_Ouput), .output_enable_2(register_output_select_4_out_10));
  register register_5 (
    .\input (d_Register_Input), .output_enable_1(register_output_select_5_out_6),
    .write(demultiplexer_1_out19), .clock(Clock), .clear(Clear), .out_2(s_register_Ouput),
    .out_1(t_register_Ouput), .output_enable_2(register_output_select_5_out_10));
  register register_6 (
    .\input (d_Register_Input), .output_enable_1(register_output_select_6_out_6),
    .write(demultiplexer_1_out23), .clock(Clock), .clear(Clear), .out_2(s_register_Ouput),
    .out_1(t_register_Ouput), .output_enable_2(register_output_select_6_out_10));
  register register_7 (
    .\input (d_Register_Input), .output_enable_1(register_output_select_7_out_6),
    .write(demultiplexer_1_out27), .clock(Clock), .clear(Clear), .out_2(s_register_Ouput),
    .out_1(t_register_Ouput), .output_enable_2(register_output_select_7_out_10));
  register register_8 (
    .\input (d_Register_Input), .output_enable_1(register_output_select_8_out_6),
    .write(demultiplexer_1_out31), .clock(Clock), .clear(Clear), .out_2(s_register_Ouput),
    .out_1(t_register_Ouput), .output_enable_2(register_output_select_8_out_10));
  register register_9 (
    .\input (d_Register_Input), .output_enable_1(register_output_select_1_out_5),
    .write(demultiplexer_1_out2), .clock(Clock), .clear(Clear), .out_2(s_register_Ouput),
    .out_1(t_register_Ouput), .output_enable_2(register_output_select_1_out_9));
  register register_10 (
    .\input (d_Register_Input), .output_enable_1(register_output_select_2_out_5),
    .write(demultiplexer_1_out6), .clock(Clock), .clear(Clear), .out_2(s_register_Ouput),
    .out_1(t_register_Ouput), .output_enable_2(register_output_select_2_out_9));
  register register_11 (
    .\input (d_Register_Input), .output_enable_1(register_output_select_3_out_5),
    .write(demultiplexer_1_out10), .clock(Clock), .clear(Clear), .out_2(s_register_Ouput),
    .out_1(t_register_Ouput), .output_enable_2(register_output_select_3_out_9));
  register register_12 (
    .\input (d_Register_Input), .output_enable_1(register_output_select_4_out_5),
    .write(demultiplexer_1_out14), .clock(Clock), .clear(Clear), .out_2(s_register_Ouput),
    .out_1(t_register_Ouput), .output_enable_2(register_output_select_4_out_9));
  register register_13 (
    .\input (d_Register_Input), .output_enable_1(register_output_select_5_out_5),
    .write(demultiplexer_1_out18), .clock(Clock), .clear(Clear), .out_2(s_register_Ouput),
    .out_1(t_register_Ouput), .output_enable_2(register_output_select_5_out_9));
  register register_14 (
    .\input (d_Register_Input), .output_enable_1(register_output_select_6_out_5),
    .write(demultiplexer_1_out22), .clock(Clock), .clear(Clear), .out_2(s_register_Ouput),
    .out_1(t_register_Ouput), .output_enable_2(register_output_select_6_out_9));
  register register_15 (
    .\input (d_Register_Input), .output_enable_1(register_output_select_7_out_5),
    .write(demultiplexer_1_out26), .clock(Clock), .clear(Clear), .out_2(s_register_Ouput),
    .out_1(t_register_Ouput), .output_enable_2(register_output_select_7_out_9));
  register register_16 (
    .\input (d_Register_Input), .output_enable_1(register_output_select_8_out_5),
    .write(demultiplexer_1_out30), .clock(Clock), .clear(Clear), .out_2(s_register_Ouput),
    .out_1(t_register_Ouput), .output_enable_2(register_output_select_8_out_9));
  register register_17 (
    .\input (d_Register_Input), .output_enable_1(register_output_select_1_out_4),
    .write(demultiplexer_1_out1), .clock(Clock), .clear(Clear), .out_2(s_register_Ouput),
    .out_1(t_register_Ouput), .output_enable_2(register_output_select_1_out_8));
  register register_18 (
    .\input (d_Register_Input), .output_enable_1(register_output_select_2_out_4),
    .write(demultiplexer_1_out5), .clock(Clock), .clear(Clear), .out_2(s_register_Ouput),
    .out_1(t_register_Ouput), .output_enable_2(register_output_select_2_out_8));
  register register_19 (
    .\input (d_Register_Input), .output_enable_1(register_output_select_3_out_4),
    .write(demultiplexer_1_out9), .clock(Clock), .clear(Clear), .out_2(s_register_Ouput),
    .out_1(t_register_Ouput), .output_enable_2(register_output_select_3_out_8));
  register register_20 (
    .\input (d_Register_Input), .output_enable_1(register_output_select_4_out_4),
    .write(demultiplexer_1_out13), .clock(Clock), .clear(Clear), .out_2(s_register_Ouput),
    .out_1(t_register_Ouput), .output_enable_2(register_output_select_4_out_8));
  register register_21 (
    .\input (d_Register_Input), .output_enable_1(register_output_select_5_out_4),
    .write(demultiplexer_1_out17), .clock(Clock), .clear(Clear), .out_2(s_register_Ouput),
    .out_1(t_register_Ouput), .output_enable_2(register_output_select_5_out_8));
  register register_22 (
    .\input (d_Register_Input), .output_enable_1(register_output_select_6_out_4),
    .write(demultiplexer_1_out21), .clock(Clock), .clear(Clear), .out_2(s_register_Ouput),
    .out_1(t_register_Ouput), .output_enable_2(register_output_select_6_out_8));
  register register_23 (
    .\input (d_Register_Input), .output_enable_1(register_output_select_7_out_4),
    .write(demultiplexer_1_out25), .clock(Clock), .clear(Clear), .out_2(s_register_Ouput),
    .out_1(t_register_Ouput), .output_enable_2(register_output_select_7_out_8));
  register register_24 (
    .\input (d_Register_Input), .output_enable_1(register_output_select_8_out_4),
    .write(demultiplexer_1_out29), .clock(Clock), .clear(Clear), .out_2(s_register_Ouput),
    .out_1(t_register_Ouput), .output_enable_2(register_output_select_8_out_8));
  register register_25 (
    .\input (d_Register_Input), .output_enable_1(register_output_select_1_out_3),
    .write(demultiplexer_1_out0), .clock(Clock), .clear(Clear), .out_2(s_register_Ouput),
    .out_1(t_register_Ouput), .output_enable_2(register_output_select_1_out_7));
  register register_26 (
    .\input (d_Register_Input), .output_enable_1(register_output_select_2_out_3),
    .write(demultiplexer_1_out4), .clock(Clock), .clear(Clear), .out_2(s_register_Ouput),
    .out_1(t_register_Ouput), .output_enable_2(register_output_select_2_out_7));
  register register_27 (
    .\input (d_Register_Input), .output_enable_1(register_output_select_3_out_3),
    .write(demultiplexer_1_out8), .clock(Clock), .clear(Clear), .out_2(s_register_Ouput),
    .out_1(t_register_Ouput), .output_enable_2(register_output_select_3_out_7));
  register register_28 (
    .\input (d_Register_Input), .output_enable_1(register_output_select_4_out_3),
    .write(demultiplexer_1_out12), .clock(Clock), .clear(Clear), .out_2(s_register_Ouput),
    .out_1(t_register_Ouput), .output_enable_2(register_output_select_4_out_7));
  register register_29 (
    .\input (d_Register_Input), .output_enable_1(register_output_select_5_out_3),
    .write(demultiplexer_1_out16), .clock(Clock), .clear(Clear), .out_2(s_register_Ouput),
    .out_1(t_register_Ouput), .output_enable_2(register_output_select_5_out_7));
  register register_30 (
    .\input (d_Register_Input), .output_enable_1(register_output_select_6_out_3),
    .write(demultiplexer_1_out20), .clock(Clock), .clear(Clear), .out_2(s_register_Ouput),
    .out_1(t_register_Ouput), .output_enable_2(register_output_select_6_out_7));
  register register_31 (
    .\input (d_Register_Input), .output_enable_1(register_output_select_7_out_3),
    .write(demultiplexer_1_out24), .clock(Clock), .clear(Clear), .out_2(s_register_Ouput),
    .out_1(t_register_Ouput), .output_enable_2(register_output_select_7_out_7));
  register register_32 (
    .\input (d_Register_Input), .output_enable_1(register_output_select_8_out_3),
    .write(demultiplexer_1_out28), .clock(Clock), .clear(Clear), .out_2(s_register_Ouput),
    .out_1(t_register_Ouput), .output_enable_2(register_output_select_8_out_7));
  register_output_select register_output_select_1 (
    .out_1(demultiplexer_3_out0), .out_2(demultiplexer_2_out0), .out_3(register_output_select_1_out_3),
    .out_4(register_output_select_1_out_4), .out_5(register_output_select_1_out_5),
    .out_6(register_output_select_1_out_6), .out_7(register_output_select_1_out_7),
    .out_8(register_output_select_1_out_8), .out_9(register_output_select_1_out_9),
    .out_10(register_output_select_1_out_10));
  register_output_select register_output_select_2 (
    .out_1(demultiplexer_3_out4), .out_2(demultiplexer_2_out4), .out_3(register_output_select_2_out_3),
    .out_4(register_output_select_2_out_4), .out_5(register_output_select_2_out_5),
    .out_6(register_output_select_2_out_6), .out_7(register_output_select_2_out_7),
    .out_8(register_output_select_2_out_8), .out_9(register_output_select_2_out_9),
    .out_10(register_output_select_2_out_10));
  register_output_select register_output_select_3 (
    .out_1(demultiplexer_3_out8), .out_2(demultiplexer_2_out8), .out_3(register_output_select_3_out_3),
    .out_4(register_output_select_3_out_4), .out_5(register_output_select_3_out_5),
    .out_6(register_output_select_3_out_6), .out_7(register_output_select_3_out_7),
    .out_8(register_output_select_3_out_8), .out_9(register_output_select_3_out_9),
    .out_10(register_output_select_3_out_10));
  register_output_select register_output_select_4 (
    .out_1(demultiplexer_3_out12), .out_2(demultiplexer_2_out12), .out_3(register_output_select_4_out_3),
    .out_4(register_output_select_4_out_4), .out_5(register_output_select_4_out_5),
    .out_6(register_output_select_4_out_6), .out_7(register_output_select_4_out_7),
    .out_8(register_output_select_4_out_8), .out_9(register_output_select_4_out_9),
    .out_10(register_output_select_4_out_10));
  register_output_select register_output_select_5 (
    .out_1(demultiplexer_3_out16), .out_2(demultiplexer_2_out16), .out_3(register_output_select_5_out_3),
    .out_4(register_output_select_5_out_4), .out_5(register_output_select_5_out_5),
    .out_6(register_output_select_5_out_6), .out_7(register_output_select_5_out_7),
    .out_8(register_output_select_5_out_8), .out_9(register_output_select_5_out_9),
    .out_10(register_output_select_5_out_10));
  register_output_select register_output_select_6 (
    .out_1(demultiplexer_3_out20), .out_2(demultiplexer_2_out20), .out_3(register_output_select_6_out_3),
    .out_4(register_output_select_6_out_4), .out_5(register_output_select_6_out_5),
    .out_6(register_output_select_6_out_6), .out_7(register_output_select_6_out_7),
    .out_8(register_output_select_6_out_8), .out_9(register_output_select_6_out_9),
    .out_10(register_output_select_6_out_10));
  register_output_select register_output_select_7 (
    .out_1(demultiplexer_3_out24), .out_2(demultiplexer_2_out24), .out_3(register_output_select_7_out_3),
    .out_4(register_output_select_7_out_4), .out_5(register_output_select_7_out_5),
    .out_6(register_output_select_7_out_6), .out_7(register_output_select_7_out_7),
    .out_8(register_output_select_7_out_8), .out_9(register_output_select_7_out_9),
    .out_10(register_output_select_7_out_10));
  register_output_select register_output_select_8 (
    .out_1(demultiplexer_3_out28), .out_2(demultiplexer_2_out28), .out_3(register_output_select_8_out_3),
    .out_4(register_output_select_8_out_4), .out_5(register_output_select_8_out_5),
    .out_6(register_output_select_8_out_6), .out_7(register_output_select_8_out_7),
    .out_8(register_output_select_8_out_8), .out_9(register_output_select_8_out_9),
    .out_10(register_output_select_8_out_10));
  Demultiplexer #(.select(5), .enable("false")) demultiplexer_2 (
    .out0(demultiplexer_2_out0[0]), .out1(demultiplexer_2_out0[1]), .out2(demultiplexer_2_out0[2]),
    .out3(demultiplexer_2_out0[3]), .out4(demultiplexer_2_out4[0]), .out5(demultiplexer_2_out4[1]),
    .out6(demultiplexer_2_out4[2]), .out7(demultiplexer_2_out4[3]), .out8(demultiplexer_2_out8[0]),
    .out9(demultiplexer_2_out8[1]), .out10(demultiplexer_2_out8[2]), .out11(demultiplexer_2_out8[3]),
    .out12(demultiplexer_2_out12[0]), .out13(demultiplexer_2_out12[1]), .out14(demultiplexer_2_out12[2]),
    .out15(demultiplexer_2_out12[3]), .out16(demultiplexer_2_out16[0]), .out17(demultiplexer_2_out16[1]),
    .out18(demultiplexer_2_out16[2]), .out19(demultiplexer_2_out16[3]), .out20(demultiplexer_2_out20[0]),
    .out21(demultiplexer_2_out20[1]), .out22(demultiplexer_2_out20[2]), .out23(demultiplexer_2_out20[3]),
    .out24(demultiplexer_2_out24[0]), .out25(demultiplexer_2_out24[1]), .out26(demultiplexer_2_out24[2]),
    .out27(demultiplexer_2_out24[3]), .out28(demultiplexer_2_out28[0]), .out29(demultiplexer_2_out28[1]),
    .out30(demultiplexer_2_out28[2]), .out31(demultiplexer_2_out28[3]), .in(read_t_register),
    .sel(t_Register_Select));
  Demultiplexer #(.select(5), .enable("false")) demultiplexer_3 (
    .out0(demultiplexer_3_out0[0]), .out1(demultiplexer_3_out0[1]), .out2(demultiplexer_3_out0[2]),
    .out3(demultiplexer_3_out0[3]), .out4(demultiplexer_3_out4[0]), .out5(demultiplexer_3_out4[1]),
    .out6(demultiplexer_3_out4[2]), .out7(demultiplexer_3_out4[3]), .out8(demultiplexer_3_out8[0]),
    .out9(demultiplexer_3_out8[1]), .out10(demultiplexer_3_out8[2]), .out11(demultiplexer_3_out8[3]),
    .out12(demultiplexer_3_out12[0]), .out13(demultiplexer_3_out12[1]), .out14(demultiplexer_3_out12[2]),
    .out15(demultiplexer_3_out12[3]), .out16(demultiplexer_3_out16[0]), .out17(demultiplexer_3_out16[1]),
    .out18(demultiplexer_3_out16[2]), .out19(demultiplexer_3_out16[3]), .out20(demultiplexer_3_out20[0]),
    .out21(demultiplexer_3_out20[1]), .out22(demultiplexer_3_out20[2]), .out23(demultiplexer_3_out20[3]),
    .out24(demultiplexer_3_out24[0]), .out25(demultiplexer_3_out24[1]), .out26(demultiplexer_3_out24[2]),
    .out27(demultiplexer_3_out24[3]), .out28(demultiplexer_3_out28[0]), .out29(demultiplexer_3_out28[1]),
    .out30(demultiplexer_3_out28[2]), .out31(demultiplexer_3_out28[3]), .in(read_s_register),
    .sel(s_Register_Select));
endmodule

module CPU (
  input  reset,
  input  clock,
  input  \wait ,
  input  [31:0] Data_in,
  output [23:0] address,
  output [31:0] Data_out,
  output read,
  output write,
  output [1:0] Data_Size,
  output trap
);

  wire and_1_out, controlled_buffer_1_out, instruction_decoder_1_add_to_pc,
       instruction_decoder_1_alu_register_override, instruction_decoder_1_cpu_address_assert,
       instruction_decoder_1_halt_clock, instruction_decoder_1_pc_in, instruction_decoder_1_pc_out,
       instruction_decoder_1_read_hi, instruction_decoder_1_read_low, instruction_decoder_1_read_register_s,
       instruction_decoder_1_read_register_t, instruction_decoder_1_register___immediate,
       instruction_decoder_1_write_hi, instruction_decoder_1_write_low,
       instruction_decoder_1_write_register_d, instruction_decoder_1_write_register_s,
       instruction_decoder_1_write_register_t, not_1_out, not_2_out, not_3_out, or_1_out;
  wire [3:0] alu_1_flag;
  wire [4:0] instruction_decoder_1_a_value, instruction_decoder_1_d_register_select,
       instruction_decoder_1_s_register_select, instruction_decoder_1_t_register_select;
  wire [5:0] instruction_decoder_1_opcode___function;
  wire [31:0] alu_1_high, alu_1_low, counter_1_pc_out_2, instruction_decoder_1_immediate,
       register_single_output_1_out, registers_1_s_register_ouput;

  Pull_Resistor pull_resistor_1 (.node(\wait ));
  or or_1 (or_1_out, \wait , instruction_decoder_1_halt_clock);
  assign controlled_buffer_1_out = not_1_out ? clock : 1'bz;  // Controlled_Buffer controlled_buffer_1
  not not_1 (not_1_out, or_1_out);
  assign controlled_buffer_1_out = or_1_out ? controlled_buffer_1_out : 1'bz;  // Controlled_Buffer controlled_buffer_2
  not not_2 (not_2_out, instruction_decoder_1_cpu_address_assert);
  and and_1 (and_1_out, not_2_out, controlled_buffer_1_out);
  not not_3 (not_3_out, and_1_out);
  register_single_output register_single_output_1 (
    .\input (Data_in), .output_enable(1'b1), .write(not_2_out), .clock(not_3_out), .clear(reset),
    .out(register_single_output_1_out));
  Counter counter_1 (
    .clock(controlled_buffer_1_out), .reset(reset), .PC_in(instruction_decoder_1_pc_in),
    .add_to_PC(instruction_decoder_1_add_to_pc), .i(instruction_decoder_1_immediate), .Mem_out(address),
    .PC_out_2(counter_1_pc_out_2), .PC_out(instruction_decoder_1_pc_out),
    .register_s(registers_1_s_register_ouput), .memoryAccess(instruction_decoder_1_cpu_address_assert));
  Instruction_Decoder instruction_decoder_1 (
    .instruction(register_single_output_1_out), .flags(alu_1_flag),
    .opcode___function(instruction_decoder_1_opcode___function), .a_value(instruction_decoder_1_a_value),
    .d_register_select(instruction_decoder_1_d_register_select),
    .t_register_select(instruction_decoder_1_t_register_select),
    .s_register_select(instruction_decoder_1_s_register_select),
    .register___immediate(instruction_decoder_1_register___immediate),
    .immediate(instruction_decoder_1_immediate), .write_register_s(instruction_decoder_1_write_register_s),
    .write_register_t(instruction_decoder_1_write_register_t),
    .write_register_d(instruction_decoder_1_write_register_d),
    .read_register_t(instruction_decoder_1_read_register_t),
    .read_register_s(instruction_decoder_1_read_register_s), .write_low(instruction_decoder_1_write_low),
    .read_low(instruction_decoder_1_read_low), .write_hi(instruction_decoder_1_write_hi),
    .read_hi(instruction_decoder_1_read_hi), .PC_in(instruction_decoder_1_pc_in),
    .add_to_PC(instruction_decoder_1_add_to_pc), .PC_out(instruction_decoder_1_pc_out),
    .halt_clock(instruction_decoder_1_halt_clock), .clock(controlled_buffer_1_out),
    .ALU_register_override(instruction_decoder_1_alu_register_override), .read(read),
    .CPU_Address_Assert(instruction_decoder_1_cpu_address_assert), .Data_Size(Data_Size), .write(write),
    .trap(trap));  // open: CPU_Data_Assert
  Registers registers_1 (
    .Clock(controlled_buffer_1_out), .d_Register_Input(counter_1_pc_out_2), .Clear(reset),
    .write_register_d(instruction_decoder_1_write_register_d),
    .d_register_select(instruction_decoder_1_d_register_select),
    .s_register_Ouput(registers_1_s_register_ouput), .t_register_Ouput(Data_out),
    .read_t_register(instruction_decoder_1_read_register_t),
    .t_Register_Select(instruction_decoder_1_t_register_select),
    .s_Register_Select(instruction_decoder_1_s_register_select),
    .read_s_register(instruction_decoder_1_read_register_s),
    .write_register_t(instruction_decoder_1_write_register_t),
    .write_register_s(instruction_decoder_1_write_register_s));
  ALU alu_1 (
    .s_register_input(registers_1_s_register_ouput), .t_register_input(Data_out),
    .immediate_input(instruction_decoder_1_immediate),
    .Opcode___function(instruction_decoder_1_opcode___function), .Flag(alu_1_flag), .High(alu_1_high),
    .Low(alu_1_low), .Output(counter_1_pc_out_2),
    .register___immediate(instruction_decoder_1_register___immediate),
    .a_value(instruction_decoder_1_a_value), .register_override(instruction_decoder_1_alu_register_override));
  register_single_output register_single_output_2 (
    .\input (alu_1_high), .output_enable(instruction_decoder_1_read_hi),
    .write(instruction_decoder_1_write_hi), .clock(controlled_buffer_1_out), .clear(reset),
    .out(counter_1_pc_out_2));
  register_single_output register_single_output_3 (
    .\input (alu_1_low), .output_enable(instruction_decoder_1_read_low),
    .write(instruction_decoder_1_write_low), .clock(controlled_buffer_1_out), .clear(reset),
    .out(counter_1_pc_out_2));

  // Notes on the sheet:
  //   control
  //   Register bank
  //   ALU
endmodule

module Instruction_Decoder (
  input  clock,
  input  [31:0] instruction,
  input  [3:0] flags,
  output [5:0] opcode___function,
  output [4:0] a_value,
  output [4:0] d_register_select,
  output [4:0] t_register_select,
  output [4:0] s_register_select,
  output register___immediate,
  output [31:0] immediate,
  output trap,
  output ALU_register_override,
  output write_register_d,
  output add_to_PC,
  output write_register_t,
  output write_register_s,
  output read_register_t,
  output read_register_s,
  output PC_out,
  output PC_in,
  output read_hi,
  output read_low,
  output write_hi,
  output write_low,
  output halt_clock,
  output read,
  output write,
  output CPU_Address_Assert,
  output CPU_Data_Assert,
  output [1:0] Data_Size
);

  wire and_1_out, and_2_out, and_3_out, and_4_out, and_5_out, and_7_out, and_8_out, and_9_out, and_10_out,
       and_11_out, and_12_out, and_13_out, and_14_out, and_15_out, and_16_out, bitselector_1_out,
       button_1_out, comparator_1_eq, demultiplexer_1_out0, demultiplexer_1_out1, demultiplexer_1_out2,
       demultiplexer_1_out3, jump_encoding, not_1_out, not_2_out, s_r_ff_1_qn, write_to_register_31;
  wire [5:0] controlled_buffer_1_out, \function ;
  wire [31:0] bit_extender_1_out, bit_extender_2_out;

  and and_1 (and_1_out, instruction[29], ~instruction[30], ~instruction[31]);  // AND_Gate
  and and_2 (and_2_out, instruction[27], ~instruction[28], ~instruction[29], ~instruction[30], ~instruction[31]);  // AND_Gate
  buf buffer_1 (write_register_t, and_1_out);
  buf buffer_2 (read_register_s, and_1_out);
  buf buffer_3 (write_register_d, and_3_out);
  buf buffer_4 (read_register_t, and_3_out);
  and and_3 (and_3_out, ~\function [3], ~\function [4], \function [5]);  // AND_Gate
  buf buffer_5 (read_register_s, and_3_out);
  buf buffer_6 (write_register_d, and_4_out);
  and and_4 (and_4_out, ~\function [5], ~\function [4], ~\function [3]);  // AND_Gate
  buf buffer_7 (read_register_s, and_4_out);
  buf buffer_8 (PC_out, and_5_out);
  buf buffer_9 (write_to_register_31, and_5_out);
  and and_5 (and_5_out, instruction[26], and_2_out);
  and and_6 (trap, ~instruction[26], instruction[27], ~instruction[28], instruction[29], instruction[30], ~instruction[31]);  // AND_Gate
  buf buffer_10 (ALU_register_override, and_7_out);
  and and_7 (and_7_out, ~instruction[31], ~instruction[30], ~instruction[29], instruction[28]);  // AND_Gate
  buf buffer_11 (read_register_t, and_7_out);
  buf buffer_12 (read_register_s, and_7_out);
  and and_8 (and_8_out, and_7_out, bitselector_1_out);
  BitSelector #(.width(4)) bitselector_1 (.in(flags), .out(bitselector_1_out), .sel(instruction[27:26]));
  assign controlled_buffer_1_out = not_1_out ? instruction[5:0] : 6'bz;  // Controlled_Buffer controlled_buffer_1
  not not_1 (not_1_out, register___immediate);
  or or_1 (jump_encoding, trap, and_2_out);
  and and_9 (and_9_out, ~\function [1], ~\function [2], \function [3], ~\function [4], ~\function [5]);  // AND_Gate
  buf buffer_13 (read_register_t, and_10_out);
  buf buffer_14 (read_register_s, and_10_out);
  buf buffer_15 (write_hi, and_10_out);
  and and_10 (and_10_out, ~register___immediate, ~\function [5], \function [4], \function [3], ~\function [2]);  // AND_Gate
  buf buffer_16 (write_low, and_10_out);
  Pull_Resistor pull_resistor_1 (.node(controlled_buffer_1_out));
  assign opcode___function = controlled_buffer_1_out | instruction[31:26];  // OR_Gate or_2, 6 bits wide
  Multiplexer #(.width(6), .enable("false")) multiplexer_1 (
    .in0(instruction[5:0]), .in1({6{1'b1}}), .out(\function ), .sel(register___immediate));
  assign bit_extender_1_out = {{16{instruction[15]}}, instruction[15:0]};  // Bit_Extender bit_extender_1
  assign bit_extender_2_out = {{6{instruction[25]}}, instruction[25:0]};  // Bit_Extender bit_extender_2
  buf buffer_17 (PC_out, and_11_out);
  and and_11 (and_11_out, \function [0], and_9_out);
  buf buffer_18 (write_to_register_31, and_11_out);
  buf buffer_19 (PC_in, and_9_out);
  buf buffer_20 (read_register_s, and_9_out);
  and and_12 (and_12_out, instruction[27], instruction[28], ~instruction[29], ~instruction[30], instruction[31]);  // AND_Gate
  and and_13 (and_13_out, ~instruction[28], instruction[29], ~instruction[30], instruction[31]);  // AND_Gate
  or or_3 (register___immediate, instruction[26], instruction[27], instruction[28], instruction[29], instruction[30], instruction[31]);
  and and_14 (and_14_out, register___immediate, ~jump_encoding);  // AND_Gate
  assign immediate = and_14_out ? bit_extender_1_out : 32'bz;  // Controlled_Buffer controlled_buffer_2
  assign immediate = jump_encoding ? bit_extender_2_out : 32'bz;  // Controlled_Buffer controlled_buffer_3
  or or_4 (add_to_PC, and_2_out, and_8_out);
  and and_15 (and_15_out, ~\function [5], \function [4], ~\function [3], ~\function [2]);  // AND_Gate
  Demultiplexer #(.select(2), .enable("false")) demultiplexer_1 (
    .out0(demultiplexer_1_out0), .out1(demultiplexer_1_out1), .out2(demultiplexer_1_out2),
    .out3(demultiplexer_1_out3), .in(and_15_out), .sel(\function [1:0]));
  buf buffer_21 (write_register_t, and_12_out);
  buf buffer_22 (read_register_t, and_12_out);
  S_R_Flip_Flop s_r_ff_1 (
    .S(and_16_out), .clk(clock), .R(not_2_out), .Qn(s_r_ff_1_qn), .reset(button_1_out), .en(clock));  // open: Q, preset
  not not_2 (not_2_out, and_16_out);
  and and_16 (and_16_out, s_r_ff_1_qn, and_13_out);
  assign Data_Size = and_16_out ? instruction[27:26] : 2'bz;  // Controlled_Buffer controlled_buffer_4
  Pull_Resistor pull_resistor_2 (.node(write_to_register_31));
  Comparator #(.width(32)) comparator_1 (.a(bit_extender_2_out), .b({32{1'b0}}), .eq(comparator_1_eq));  // open: gt, lt
  buf buffer_23 (read_hi, demultiplexer_1_out0);
  buf buffer_24 (write_register_d, demultiplexer_1_out0);
  buf buffer_25 (write_hi, demultiplexer_1_out1);
  buf buffer_26 (read_register_s, demultiplexer_1_out1);
  buf buffer_27 (write_register_d, demultiplexer_1_out2);
  buf buffer_28 (read_low, demultiplexer_1_out2);
  buf buffer_29 (read_register_s, demultiplexer_1_out3);
  buf buffer_30 (write_low, demultiplexer_1_out3);
  Button button_1 (.out(button_1_out));
  buf buffer_31 (read_register_t, and_16_out);
  buf buffer_32 (read_register_s, and_16_out);
  buf buffer_33 (write, and_16_out);
  buf buffer_34 (write_register_d, write_to_register_31);
  Multiplexer #(.width(5), .enable("false")) multiplexer_2 (
    .in0(instruction[15:11]), .in1({5{1'b1}}), .out(d_register_select), .sel(write_to_register_31));
  Pull_Resistor pull_resistor_3 (.node(immediate));
  and and_17 (halt_clock, comparator_1_eq, trap);
  or or_5 (CPU_Address_Assert, read, write);
  Pull_Resistor pull_resistor_4 (.node(trap));
  Pull_Resistor pull_resistor_5 (.node(ALU_register_override));
  Pull_Resistor pull_resistor_6 (.node(write_register_d));
  Pull_Resistor pull_resistor_7 (.node(write_register_t));
  Pull_Resistor pull_resistor_8 (.node(write_register_s));
  Pull_Resistor pull_resistor_9 (.node(read_register_t));
  Pull_Resistor pull_resistor_10 (.node(read_register_s));
  Pull_Resistor pull_resistor_11 (.node(PC_out));
  Pull_Resistor pull_resistor_12 (.node(PC_in));
  Pull_Resistor pull_resistor_13 (.node(read_hi));
  Pull_Resistor pull_resistor_14 (.node(read_low));
  Pull_Resistor pull_resistor_15 (.node(write_hi));
  Pull_Resistor pull_resistor_16 (.node(write_low));
  Pull_Resistor pull_resistor_17 (.node(halt_clock));
  Pull_Resistor pull_resistor_18 (.node(read));
  Pull_Resistor pull_resistor_19 (.node(write));
  Pull_Resistor pull_resistor_20 (.node(CPU_Address_Assert));
  Pull_Resistor pull_resistor_21 (.node(CPU_Address_Assert));
  Pull_Resistor pull_resistor_22 (.node(Data_Size));

  assign a_value = instruction[10:6];
  assign CPU_Data_Assert = CPU_Address_Assert;
  assign s_register_select = instruction[25:21];
  assign t_register_select = instruction[20:16];

  // Other names for the same wires on the sheet: opcode[5:0] = instruction[31:26]

  // Notes on the sheet:
  //   j / jal
  //   sll / srl / sra / sllv / srlv / srav
  //   trap
  //   buffer_1 drives only 1 and floats otherwise
  //   buffer_2 drives only 1 and floats otherwise
  //   buffer_3 drives only 1 and floats otherwise
  //   buffer_4 drives only 1 and floats otherwise
  //   buffer_5 drives only 1 and floats otherwise
  //   buffer_6 drives only 1 and floats otherwise
  //   buffer_7 drives only 1 and floats otherwise
  //   buffer_8 drives only 1 and floats otherwise
  //   buffer_9 drives only 1 and floats otherwise
  //   branch instructions
  //   mult / divi
  //   buffer_10 drives only 1 and floats otherwise
  //   buffer_11 drives only 1 and floats otherwise
  //   buffer_12 drives only 1 and floats otherwise
  //   jr / jalr
  //   buffer_13 drives only 1 and floats otherwise
  //   buffer_14 drives only 1 and floats otherwise
  //   buffer_15 drives only 1 and floats otherwise
  //   buffer_16 drives only 1 and floats otherwise
  //   llo / lhi
  //   sb / shw / sw
  //   buffer_17 drives only 1 and floats otherwise
  //   buffer_18 drives only 1 and floats otherwise
  //   buffer_19 drives only 1 and floats otherwise
  //   buffer_20 drives only 1 and floats otherwise
  //   mfhi / mflo / mthi / mt lo
  //   buffer_21 drives only 1 and floats otherwise
  //   buffer_22 drives only 1 and floats otherwise
  //   buffer_23 drives only 1 and floats otherwise
  //   buffer_24 drives only 1 and floats otherwise
  //   buffer_25 drives only 1 and floats otherwise
  //   buffer_26 drives only 1 and floats otherwise
  //   buffer_27 drives only 1 and floats otherwise
  //   buffer_28 drives only 1 and floats otherwise
  //   buffer_29 drives only 1 and floats otherwise
  //   buffer_30 drives only 1 and floats otherwise
  //   buffer_31 drives only 1 and floats otherwise
  //   buffer_32 drives only 1 and floats otherwise
  //   buffer_33 drives only 1 and floats otherwise
  //   buffer_34 drives only 1 and floats otherwise
  //   0 byte 1 hword 3 word
endmodule

module ALU (
  input  [31:0] s_register_input,
  input  [31:0] t_register_input,
  input  [31:0] immediate_input,
  input  register_override,
  input  register___immediate,
  input  [5:0] Opcode___function,
  input  [4:0] a_value,
  output [3:0] Flag,
  output [31:0] Low,
  output [31:0] High,
  output [31:0] Output
);

  wire and_1_out, and_2_out, and_3_out, and_4_out, and_6_out, bitselector_1_out, comparator_2_eq, not_1_out,
       not_4_out, not_5_out, or_1_out;
  wire [31:0] adder_1_out, and_5_out, controlled_buffer_1_out, divider_1_out, divider_1_rem,
       multiplier_1_cout, multiplier_1_out, nor_1_out, or_3_out, subtractor_1_out, xor_1_out;

  assign controlled_buffer_1_out = not_1_out ? t_register_input : 32'bz;  // Controlled_Buffer controlled_buffer_1
  not not_1 (not_1_out, and_1_out);
  assign controlled_buffer_1_out = and_1_out ? immediate_input : 32'bz;  // Controlled_Buffer controlled_buffer_2
  and and_1 (and_1_out, ~register_override, register___immediate);  // AND_Gate
  and and_2 (and_2_out, register___immediate, Opcode___function[3], ~Opcode___function[4], ~Opcode___function[5]);  // AND_Gate
  and and_3 (and_3_out, ~register___immediate, ~Opcode___function[4], Opcode___function[5]);  // AND_Gate
  and and_4 (and_4_out, ~Opcode___function[1], ~Opcode___function[2], Opcode___function[3], Opcode___function[4], ~Opcode___function[5], register___immediate);  // AND_Gate
  Pull_Resistor pull_resistor_1 (.node(s_register_input));
  Pull_Resistor pull_resistor_2 (.node(controlled_buffer_1_out));
  or or_1 (or_1_out, and_2_out, and_3_out);
  Comparator #(.width(32)) comparator_1 (
    .a(s_register_input), .b(controlled_buffer_1_out), .eq(Flag[0]));  // open: gt, lt
  Comparator #(.width(32)) comparator_2 (.a(s_register_input), .b({32{1'b0}}), .eq(comparator_2_eq));  // open: gt, lt
  BitSelector #(.width(32)) bitselector_1 (.in(s_register_input), .out(bitselector_1_out), .sel({5{1'b1}}));
  not not_2 (Flag[1], Flag[0]);
  or or_2 (Flag[2], bitselector_1_out, comparator_2_eq);
  Divider #(.width(32)) divider_1 (
    .a(s_register_input), .b(controlled_buffer_1_out), .out(divider_1_out), .rem(divider_1_rem));  // open: upper
  Multiplier #(.width(32)) multiplier_1 (
    .a(s_register_input), .b(controlled_buffer_1_out), .out(multiplier_1_out), .cout(multiplier_1_cout));  // open: cin
  Adder #(.width(32)) adder_1 (
    .a(s_register_input), .b(controlled_buffer_1_out), .out(adder_1_out));  // open: cin, cout
  Subtractor #(.width(32)) subtractor_1 (
    .a(s_register_input), .b(controlled_buffer_1_out), .out(subtractor_1_out));  // open: bin, bout
  assign and_5_out = s_register_input & controlled_buffer_1_out;  // AND_Gate and_5, 32 bits wide
  assign or_3_out = s_register_input | controlled_buffer_1_out;  // OR_Gate or_3, 32 bits wide
  assign xor_1_out = s_register_input ^ controlled_buffer_1_out;  // XOR_Gate xor_1, 32 bits wide
  assign nor_1_out = ~(s_register_input | controlled_buffer_1_out);  // NOR_Gate nor_1, 32 bits wide
  shift_unit shift_unit_1 (
    .opcode(Opcode___function), .t_register(s_register_input), .a_value(a_value),
    .s_register(controlled_buffer_1_out), .register___immedate(register___immediate), .\output (Output));
  not not_3 (Flag[3], Flag[2]);
  Multiplexer #(.width(16)) multiplexer_1 (
    .in0(controlled_buffer_1_out[15:0]), .in1(s_register_input[15:0]), .out(Output[15:0]),
    .sel(Opcode___function[0]), .en(and_4_out));
  not not_4 (not_4_out, Opcode___function[0]);
  Multiplexer #(.width(16)) multiplexer_2 (
    .in0(controlled_buffer_1_out[31:16]), .in1(s_register_input[31:16]), .out(Output[31:16]),
    .sel(not_4_out), .en(and_4_out));
  and and_6 (and_6_out, ~register___immediate, ~Opcode___function[5], Opcode___function[4], Opcode___function[3], ~Opcode___function[2]);  // AND_Gate
  not not_5 (not_5_out, Opcode___function[1]);
  Multiplexer #(.width(32)) multiplexer_3 (
    .in0(divider_1_out), .in1(multiplier_1_out), .out(Low), .sel(not_5_out), .en(and_6_out));
  Multiplexer #(.width(32)) multiplexer_4 (
    .in0(divider_1_rem), .in1(multiplier_1_cout), .out(High), .sel(not_5_out), .en(and_6_out));
  Multiplexer #(.select(3), .width(32)) multiplexer_5 (
    .in0(adder_1_out), .in1(adder_1_out), .in2(subtractor_1_out), .in3(subtractor_1_out), .in4(and_5_out),
    .in5(or_3_out), .in6(xor_1_out), .in7(nor_1_out), .out(Output), .sel(Opcode___function[2:0]),
    .en(or_1_out));

  // Other names for the same wires on the sheet: code_0_2[2:0] = Opcode___function[2:0];
  //   code_3_5[2:0] = Opcode___function[5:3]

  // Notes on the sheet:
  //   100 register alu functions
  //   001 immediate alu functions
endmodule

module register (
  input  output_enable_2,
  input  [31:0] \input ,
  input  output_enable_1,
  input  write,
  input  clock,
  input  clear,
  output [31:0] out_1,
  output [31:0] out_2
);

  wire [31:0] register_1_q;

  Register #(.width(32), .trigger("falling")) register_1 (
    .D(\input ), .en(write), .Q(register_1_q), .clk(clock), .clr(clear));
  assign out_1 = output_enable_2 ? register_1_q : 32'bz;  // Controlled_Buffer controlled_buffer_1
  Pull_Resistor pull_resistor_1 (.node(output_enable_2));
  assign out_2 = output_enable_1 ? register_1_q : 32'bz;  // Controlled_Buffer controlled_buffer_2
  Pull_Resistor pull_resistor_2 (.node(output_enable_1));
endmodule

module register_output_select (
  input  [3:0] out_1,
  input  [3:0] out_2,
  output out_3,
  output out_4,
  output out_5,
  output out_6,
  output out_7,
  output out_8,
  output out_9,
  output out_10
);


  assign out_3 = out_1[0];
  assign out_4 = out_1[1];
  assign out_5 = out_1[2];
  assign out_6 = out_1[3];
  assign out_7 = out_2[0];
  assign out_8 = out_2[1];
  assign out_9 = out_2[2];
  assign out_10 = out_2[3];
endmodule

module register_single_output (
  input  [31:0] \input ,
  input  output_enable,
  input  write,
  input  clock,
  input  clear,
  output [31:0] out
);

  wire [31:0] register_1_q;

  Register #(.width(32), .trigger("falling")) register_1 (
    .D(\input ), .en(write), .Q(register_1_q), .clk(clock), .clr(clear));
  assign out = output_enable ? register_1_q : 32'bz;  // Controlled_Buffer controlled_buffer_1
  Pull_Resistor pull_resistor_1 (.node(output_enable));
endmodule

module Counter (
  input  clock,
  input  PC_in,
  input  add_to_PC,
  input  reset,
  input  PC_out,
  input  memoryAccess,
  input  [31:0] i,
  input  [31:0] register_s,
  output [31:0] PC_out_2,
  output [23:0] Mem_out
);

  wire not_1_out, not_2_out, not_3_out, or_1_out, or_2_out, or_3_out;
  wire [0:0] or_4_out;
  wire [23:0] bit_extender_4_out, bit_extender_5_out;
  wire [29:0] adder_1_out, adder_2_out, bit_extender_3_out, controlled_buffer_1_out, controlled_buffer_2_out,
       counter_1_q, multiplexer_1_out, pull_resistor_1_node, register_s_t, undriven, value_i;
  wire [31:0] shifter_1_out;

  Pull_Resistor pull_resistor_1 (.node(pull_resistor_1_node));
  Shifter #(.width(32), .shift("lr")) shifter_1 (.in(register_s), .\dist (5'b00010), .out(shifter_1_out));
  Adder #(.width(30)) adder_1 (.a(pull_resistor_1_node), .b(undriven), .out(adder_1_out), .cin(1'b1));  // open: cout
  not not_1 (not_1_out, or_1_out);
  or or_1 (or_1_out, PC_in, add_to_PC);
  or or_2 (or_2_out, clock, memoryAccess);
  assign controlled_buffer_1_out = add_to_PC ? value_i : 30'bz;  // Controlled_Buffer controlled_buffer_1
  Bit_Extender #(.in_width(32), .out_width(30)) bit_extender_1 (.in(i), .out(value_i));
  Bit_Extender #(.in_width(32), .out_width(30)) bit_extender_2 (.in(shifter_1_out), .out(register_s_t));
  Bit_Extender #(.in_width(32), .out_width(30)) bit_extender_3 (.in(register_s), .out(bit_extender_3_out));
  not not_2 (not_2_out, or_3_out);
  assign controlled_buffer_2_out = not_2_out ? counter_1_q : 30'bz;  // Controlled_Buffer controlled_buffer_2
  Counter_part #(.width(30), .max('h3fffffff)) counter_1 (
    .load(or_1_out), .D(adder_2_out), .count(not_1_out), .Q(counter_1_q), .clk(or_2_out), .clr(reset));  // open: carry
  Pull_Resistor pull_resistor_2 (.node(controlled_buffer_1_out));
  assign controlled_buffer_2_out = memoryAccess ? value_i : 30'bz;  // Controlled_Buffer controlled_buffer_3
  Pull_Resistor pull_resistor_3 (.node(controlled_buffer_2_out));
  assign controlled_buffer_1_out = PC_in ? register_s_t : 30'bz;  // Controlled_Buffer controlled_buffer_4
  assign controlled_buffer_1_out = memoryAccess ? bit_extender_3_out : 30'bz;  // Controlled_Buffer controlled_buffer_5
  or or_3 (or_3_out, memoryAccess, PC_in);
  Adder #(.width(30)) adder_2 (
    .a(controlled_buffer_2_out), .b(controlled_buffer_1_out), .out(adder_2_out));  // open: cin, cout
  or or_4 (or_4_out[0], add_to_PC, memoryAccess);
  assign PC_out_2 = PC_out ? {counter_1_q, 2'b00} : 32'bz;  // Controlled_Buffer controlled_buffer_6
  Multiplexer #(.select(2), .width(30), .enable("false")) multiplexer_1 (
    .in0(counter_1_q), .in1(adder_2_out), .in2(register_s_t), .out(multiplexer_1_out),
    .sel({PC_in, or_4_out[0]}));  // open: in3
  Bit_Extender #(.in_width(32), .out_width(24)) bit_extender_4 (
    .in({multiplexer_1_out, 2'b00}), .out(bit_extender_4_out));
  Bit_Extender #(.in_width(30), .out_width(24)) bit_extender_5 (.in(multiplexer_1_out), .out(bit_extender_5_out));
  assign Mem_out = not_3_out ? bit_extender_4_out : 24'bz;  // Controlled_Buffer controlled_buffer_7
  not not_3 (not_3_out, memoryAccess);
  assign Mem_out = memoryAccess ? bit_extender_5_out : 24'bz;  // Controlled_Buffer controlled_buffer_8

  // Other names for the same wires on the sheet: s___i = memoryAccess
endmodule

module shift_unit (
  input  [5:0] opcode,
  input  [31:0] t_register,
  input  register___immedate,
  input  [4:0] a_value,
  input  [31:0] s_register,
  output [31:0] \output 
);

  wire and_1_out, and_2_out;
  wire [4:0] bit_extender_1_out, multiplexer_1_out;
  wire [31:0] shifter_1_out, shifter_2_out, shifter_3_out;

  Bit_Extender #(.in_width(32), .out_width(5)) bit_extender_1 (.in(s_register), .out(bit_extender_1_out));
  Multiplexer #(.width(5), .enable("false")) multiplexer_1 (
    .in0(a_value), .in1(bit_extender_1_out), .out(multiplexer_1_out), .sel(opcode[2]));
  Shifter #(.width(32)) shifter_1 (.in(t_register), .\dist (multiplexer_1_out), .out(shifter_1_out));
  Shifter #(.width(32), .shift("lr")) shifter_2 (.in(t_register), .\dist (multiplexer_1_out), .out(shifter_2_out));
  Shifter #(.width(32), .shift("ar")) shifter_3 (.in(t_register), .\dist (multiplexer_1_out), .out(shifter_3_out));
  and and_1 (and_1_out, ~opcode[5], ~opcode[4], ~opcode[3]);  // AND_Gate
  and and_2 (and_2_out, and_1_out, ~register___immedate);  // AND_Gate
  Multiplexer #(.select(2), .width(32)) multiplexer_2 (
    .in0(shifter_1_out), .in2(shifter_2_out), .in3(shifter_3_out), .out(\output ), .sel(opcode[1:0]),
    .en(and_2_out));  // open: in1

  // Other names for the same wires on the sheet: register___a = opcode[2]
endmodule
